# Fritzing sketch 5_servo_joystick_schematic (saved by Fritzing 0.9.6b)
breadboards: 1

parts:
  Part1 = Arduino Uno (Rev3) - ICSP
  Part2 = Thumb Joystick
  VCC1 = 4 x AAA Battery Mount
  J1 = Basic Servo
  J2 = Basic Servo
  J3 = Basic Servo
  J4 = Basic Servo
  J5 = Basic Servo

nets:
  N1: Part1.A0, Part2.VERT
  N2: Part1.A1, Part2.HORZ
  N3: Part1.ICSP_MISO, Part1.D12/MISO, J2.pulse
  N4: Part1.D9_PWM, J5.pulse
  N5: Part1.D10_PWM/SS, J4.pulse
  N6: Part1.D11_PWM/MOSI, J3.pulse
  N7: Part1.D13/SCK, J1.pulse
  N8: Part1.D6_PWM, Part2.SEL
  5V: Part1.5V, Part2.VCC
  GND: Part1.GND, Part2.GND, VCC1.-, J1.gnd, J2.gnd, J3.gnd, J4.gnd, J5.gnd
  VCC: VCC1.+, J1.vcc, J2.vcc, J3.vcc, J4.vcc, J5.vcc

notes:
  Servo's are connected to external 5v power supply, this requires a common ground connected to the arduino
  this joystick module is not a direct copy of the one used in the project but the color coded wires are connected in the same way as the finishedproject
  the breadboard here only functions as an easy way to demonstrate the power connections, as on my finished project i used an arduino protoshield
  this 5v power suply is actualy a hard wired usb cable in my project to facilitate easy connection to a usb power bank
